# Fritzing sketch 03_led_and_button (saved by Fritzing 0.9.1b)
breadboards: 1

parts:
  Part1 = Arduino Uno (Rev3)
  S1 = Pushbutton [package="[THT]"]
  R1 = Resistor [tolerance=±5% resistance=10k package=THT]
  LED1 = LED - 5mm [color="Red (633nm)" package="5 mm [THT]"]
  R2 = Resistor [tolerance=±5% resistance=330 package=THT]

nets:
  N1: Part1.D11_PWM/MOSI, S1.Pin_3, S1.Pin_4, R1.Pin_0
  N2: Part1.D5_PWM, LED1.cathode
  N3: Part1.5V, R1.Pin_1
  N4: Part1.GND, S1.Pin_1, S1.Pin_2, R2.Pin_1
  N5: LED1.anode, R2.Pin_0
